// Logisim project Lab3_multiplexer.circ as structural Verilog: 1 circuit, main circuit main
module main (
  input  s0,
  input  s1,
  input  s2
);

  wire and_1_out, and_2_out, and_3_out, and_4_out, and_5_out, and_6_out, and_7_out, and_8_out, not_1_out,
       not_2_out, not_3_out, or_1_out, or_2_out, or_3_out;

  not not_1 (not_1_out, s0);
  not not_2 (not_2_out, s1);
  not not_3 (not_3_out, s2);
  and and_1 (and_1_out, not_1_out, not_2_out, not_3_out, 1'b1);
  and and_2 (and_2_out, not_1_out, not_2_out, s2, 1'b1);
  and and_3 (and_3_out, not_1_out, s1, not_3_out, 1'b1);
  and and_4 (and_4_out, not_1_out, s1, s2, 1'b1);
  and and_5 (and_5_out, s0, not_2_out, not_3_out, 1'b1);
  and and_6 (and_6_out, s0, not_2_out, s2, 1'b1);
  and and_7 (and_7_out, s0, s1, not_3_out, 1'b1);
  and and_8 (and_8_out, s0, s1, s2, 1'b1);
  or or_1 (or_1_out, and_1_out, and_2_out, and_3_out, and_4_out, and_5_out);
  or or_2 (or_2_out, and_6_out, and_7_out, and_8_out);
  or or_3 (or_3_out, or_1_out, or_2_out);
  LED led_1 (.in(or_3_out));
endmodule
