// Logisim project encoder.circ as structural Verilog: 1 circuit, main circuit main
module main (
);

  wire button_1_out, button_2_out, button_3_out, button_5_out, button_6_out, button_7_out, button_8_out,
       nor_1_out, or_1_out, or_2_out;

  Button button_1 (.out(button_1_out));
  Button button_2 (.out(button_2_out));
  Button button_3 (.out(button_3_out));
  Button button_4 ();  // open: out
  Button button_5 (.out(button_5_out));
  Button button_6 (.out(button_6_out));
  Button button_7 (.out(button_7_out));
  Button button_8 (.out(button_8_out));
  nor nor_1 (nor_1_out, button_5_out, button_3_out, button_2_out, button_1_out);
  or or_1 (or_1_out, button_3_out, button_5_out, button_7_out, button_8_out);
  or or_2 (or_2_out, button_2_out, button_5_out, button_6_out, button_8_out);
  LED led_1 (.in(nor_1_out));
  LED led_2 (.in(or_1_out));
  LED led_3 (.in(or_2_out));

  // Notes on the sheet:
  //   i0
  //   i1
  //   i2
  //   i3
  //   i4
  //   i5
  //   i6
  //   i7
endmodule
